# Fritzing sketch stablizing spoon (saved by Fritzing 0.8.7b)
breadboards: 1

parts:
  SERVO1 = Tower Pro SG90 servo [part_number=101246]
  GY1 = GY-521 (MPU-6050) [form="♀ (female)" package=THT]
  Part1 = Arduino Uno (Rev3)
  SW-1 = Vibration sensor module
  Part2 = Bluetooth HC-05 Macho
  SERVO2 = Tower Pro SG90 servo [part_number=101246]

nets:
  N1: SERVO1.Signal, Part1.D11_PWM/MOSI
  +5V: SERVO1.+5V, GY1.pin1, Part1.5V, SW-1.vcc, Part2.VCC, SERVO2.+5V
  GND: SERVO1.GND, GY1.pin2, Part1.GND, SW-1.Ground, Part2.GND, SERVO2.GND
  N2: GY1.pin3, Part1.A5/SCL
  N3: GY1.pin4, Part1.A4/SDA
  N4: GY1.pin8, Part1.D2
  N5: Part1.A0, SW-1.Digital_output
  N6: Part1.D10_PWM/SS, SERVO2.Signal
  N7: Part1.D3_PWM, Part2.RXD
  N8: Part1.D4, Part2.TXD

custom parts:
  Tower Pro SG90 servo: Original file by John De Cristofaro http://www.adafruit.com/products/1449 Adafruit Feedback Servo (Small) Edited by: e-radionica.com 28/9/2015
  GY-521 (MPU-6050): Placa GY-521 basada en conjunto de acelerómetro+giroscopios MPU-6050
  Vibration sensor module: Single-roller type full induction trigger switch. When no vibration or tilt, the product is ON conduction state, and in the steady state, when a vibration or tilt, the switch will be rendered instantly disconnect the conductive resistance increases, generating a current pulse signal, thereby triggering circuit. The default state of the swith is close Digital output Supply voltage:3.3V-5V On-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
