# Fritzing sketch bluetooh_vibration (saved by Fritzing 0.8.7b)
breadboards: 1

parts:
  Part1 = Arduino Uno (Rev3)
  Part2 = Bluetooth HC-05 Macho
  SW-1 = Vibration sensor module

nets:
  N1: Part1.A0, SW-1.Digital_output
  N2: Part1.D3_PWM, Part2.RXD
  N3: Part1.D4, Part2.TXD
  VCC: Part1.5V, Part2.VCC, SW-1.vcc
  GND: Part1.GND, Part2.GND, SW-1.Ground

custom parts:
  Vibration sensor module: Single-roller type full induction trigger switch. When no vibration or tilt, the product is ON conduction state, and in the steady state, when a vibration or tilt, the switch will be rendered instantly disconnect the conductive resistance increases, generating a current pulse signal, thereby triggering circuit. The default state of the swith is close Digital output Supply voltage:3.3V-5V On-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
