# Fritzing sketch Spoon (saved by Fritzing 0.8.7b)
breadboards: 1

parts:
  SERVO1 = Tower Pro SG90 servo [part_number=101246]
  SERVO2 = Tower Pro SG90 servo [part_number=101246]
  GY1 = GY-521 (MPU-6050) [form="♀ (female)" package=THT]
  Part1 = Arduino Uno (Rev3)

nets:
  N1: SERVO1.Signal, Part1.D11_PWM/MOSI
  +5V: SERVO1.+5V, SERVO2.+5V, GY1.pin1, Part1.5V
  GND: SERVO1.GND, SERVO2.GND, Part1.GND
  N2: SERVO2.Signal, Part1.D10_PWM/SS
  N3: GY1.pin3, Part1.A5/SCL
  N4: GY1.pin4, Part1.A4/SDA
  N5: GY1.pin8, Part1.D2

custom parts:
  Tower Pro SG90 servo: Original file by John De Cristofaro http://www.adafruit.com/products/1449 Adafruit Feedback Servo (Small) Edited by: e-radionica.com 28/9/2015
  GY-521 (MPU-6050): Placa GY-521 basada en conjunto de acelerómetro+giroscopios MPU-6050
